# Fritzing sketch Debounce_w_433Mhz_and_555Timer (saved by Fritzing 1.0.3b)
circuit board: 7cm x 4cm
breadboards: 1

parts:
  R3 = Resistor [tolerance=±5% power=0.25W resistance=1k package=THT]
  C2 = Ceramic Capacitor [capacitance=10nF voltage=35V package="100 mil [THT, multilayer]"]
  555_Timer = 555 Timer [package="DIP8 [THT]"]
  S1 = Pushbutton [package="[THT]"]
  Q1 = NPN-Transistor [package="TO92 [THT]"]
  R1 = Resistor [tolerance=±5% power=0.25W resistance=460k package=THT]
  QIACHIP_RX480E = male pin header, 7 pins [form="♂ (male)"]
  U2_5v = Voltage Regulator - 5V [package="TO220 [THT]"]
  R5 = Resistor [tolerance=±5% power=0.25W resistance=10k package=THT]
  C3 = Ceramic Capacitor [capacitance=0.1µF voltage=35V package="100 mil [THT, multilayer]"]
  R6 = Resistor [tolerance=±5% power=0.25W resistance=220 package=THT]
  D1 = Rectifier Diode [part_number=1N4001 package="300 mil [THT]"]
  ext_Switch = molex pin header, 2 pins [form=molex]
  3v_GPIO_IN = molex pin header, 2 pins [form=molex]
  vOUT_3_3v = molex pin header, 2 pins [form=molex]
  vIN_9-12v = molex pin header, 2 pins [form=molex]
  D2 = Rectifier Diode [part_number=1N4001 package="300 mil [THT]"]
  C4 = Ceramic Capacitor [capacitance=0.1µF voltage=35V package="100 mil [THT, multilayer]"]
  VCC1 = Battery block 9V [internal_resistance=0.1Ω]
  U4_3_3v = Voltage Regulator -- 3.3 V -- LM1117

nets:
  N1: R3.Pin_0, 555_Timer.Trigger, 555_Timer.Threshold, R5.Pin_0, C3.0
  N2: R3.Pin_1, S1.Pin_3, S1.Pin_4, Q1.C, ext_Switch.pin1
  GND: C2.0, 555_Timer.Ground, S1.Pin_1, S1.Pin_2, Q1.E, QIACHIP_RX480E.pin1, U2_5v.GND, C3.1, ext_Switch.pin2, 3v_GPIO_IN.pin2, vOUT_3_3v.pin2, vIN_9-12v.pin2, C4.0, VCC1.-, U4_3_3v.GND
  N3: C2.1, 555_Timer.Control_Voltage
  N4: 555_Timer.Output, U4_3_3v.IN
  N5: 555_Timer.Reset, 555_Timer.Vcc_Supply_Voltage, U2_5v.input_voltage, R5.Pin_1, vIN_9-12v.pin1, VCC1.+
  N6: Q1.B, R1.Pin_1
  N7: R1.Pin_0, D1.cathode, D2.cathode
  N8: QIACHIP_RX480E.pin2, R6.Pin_0
  N9: QIACHIP_RX480E.pin4, D1.anode
  N10: U2_5v.output_voltage, R6.Pin_1
  N11: 3v_GPIO_IN.pin1, D2.anode
  N12: vOUT_3_3v.pin1, C4.1, U4_3_3v.OUT

notes:
  +
  -
  Debounce v1.0

custom parts:
  Voltage Regulator -- 3.3 V -- LM1117: LM1117-3.3 Voltage regulator, 3.3 V output. Note that the pinout order is not the same as LM7805 or LM7833.
